# Fritzing sketch Garage (saved by Fritzing 0.9.3b)
breadboards: 1

parts:
  SparkFun_Pro_Micro1 = SparkFun Pro Micro [part_number=DEV-12640]
  Part1 = Photon
  Stepper_Driver = ULN2003A breakout board
  LD1 = LD
  Internal_Light = LEDs [package=led10mm]
  Rotary_Encoder = ENCODER-QUADRATURE [package=encoder-16mm-quad]
  JP1 = Header 12 [package=1x12_machine-pin-header_lock.004]
  BATT1 = 4xAA Switchable Battery Pack w/Bare Wire
  Down_Switch_(Back) = D2F-FL Omron Snap Action Limit Switch with Level
  Up_Switch_(Front) = D2F-FL Omron Snap Action Limit Switch with Level
  JP2 = Header 12 [package=1x12_machine-pin-header_lock.004]
  JP3 = Header 12 [package=1x12_machine-pin-header_lock.004]
  JP4 = Header 12 [package=1x12_machine-pin-header_lock.004]
  Laser_Detector = Dagu DGServo 9g header connector (female) [package=THT]
  R1 = Resistor [tolerance=±5% resistance=180 package="0402 [SMD]"]
  Button = Pushbutton [package="[THT]"]

nets:
  APM RAW: SparkFun_Pro_Micro1.RAW, JP1.12
  GND: SparkFun_Pro_Micro1.GND, Part1.GND, Stepper_Driver.0V, LD1.cathode, Rotary_Encoder.C, JP1.11, BATT1.NEG, Down_Switch_(Back).COM, Up_Switch_(Front).COM, JP2.2, JP3.4, JP4.9, JP4.10, Laser_Detector.gnd, R1.Pin_0, Button.Pin_3, Button.Pin_4
  APM RST: SparkFun_Pro_Micro1.RESET, JP1.10
  Vcc: SparkFun_Pro_Micro1.VCC, Part1.VIN, LD1.anode, JP1.9, JP2.1, Laser_Detector.Vcc
  APM A3: SparkFun_Pro_Micro1.A3, Stepper_Driver.In_4, JP1.8
  APM A2: SparkFun_Pro_Micro1.A2, Stepper_Driver.In_2, JP1.7
  APM A1: SparkFun_Pro_Micro1.A1, Stepper_Driver.In_3, JP1.6
  APM A0: SparkFun_Pro_Micro1.A0, Stepper_Driver.In_1, JP1.5
  APM D15: SparkFun_Pro_Micro1.SCK, Rotary_Encoder.B, JP1.4
  APM D14: SparkFun_Pro_Micro1.MISO, JP1.3, Up_Switch_(Front).NO
  APM D16: SparkFun_Pro_Micro1.MOSI, JP1.2, Down_Switch_(Back).NO
  APM D10: SparkFun_Pro_Micro1.D10, JP1.1, Laser_Detector.pulse
  APM D9: SparkFun_Pro_Micro1.D9, Internal_Light.A, JP4.1
  APM D8: SparkFun_Pro_Micro1.D8, JP4.2, Button.Pin_1, Button.Pin_2
  APM D7: SparkFun_Pro_Micro1.D7, JP4.3
  APM D6: SparkFun_Pro_Micro1.D6, JP4.4
  APM D5: SparkFun_Pro_Micro1.D5, JP4.5
  APM D4: SparkFun_Pro_Micro1.D4, JP4.6
  APM D3: SparkFun_Pro_Micro1.D3, JP4.7
  APM D2: SparkFun_Pro_Micro1.D2, JP4.8
  APM RX: SparkFun_Pro_Micro1.RXI, Part1.TX, JP2.3, JP4.11
  APM TX: SparkFun_Pro_Micro1.TXO, Part1.RX, JP2.4, JP4.12
  N1: Part1.A0, JP2.12
  N2: Part1.A1, JP2.11
  N3: Part1.A2, JP2.10
  N4: Part1.A3, JP2.9
  N5: Part1.A4, JP2.8
  N6: Part1.A5, JP2.7
  N7: Part1.DAC, JP2.6
  N8: Part1.WKP, JP2.5
  N9: Part1.D0, JP3.12
  N10: Part1.D1, JP3.11
  N11: Part1.D2, JP3.10
  N12: Part1.D3, JP3.9
  N13: Part1.D4, JP3.8
  N14: Part1.D5, JP3.7
  N15: Part1.D6, JP3.6
  N16: Part1.D7, JP3.5
  P VBAT: Part1.VBAT, JP3.3
  P RST: Part1.RST, JP3.2
  P 3V3: Part1.3V3, JP3.1
  N17: Stepper_Driver.+5V, BATT1.POS
  N18: Internal_Light.C, R1.Pin_1

custom parts:
  SparkFun Pro Micro: This tiny little board does all of the neat-o Arduino tricks that you’re familiar with: 4 channels of 10-bit ADC, 5 PWM pins, 12 DIOs as well as hardware serial connections Rx and Tx. Running at 16MHz and 5V, this board will remind you a lot of your other favorite Arduino-compatible boards but this little guy can go just about anywhere. There is a voltage regulator on board so it can accept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
  ULN2003A breakout board: ULN2003A 7-way Darlington Transistor Driver on breakoutboard
  LD: A Generic Red Dot Laser Diode Module (~5mW)
  4xAA Switchable Battery Pack w/Bare Wire: 4xAA Switchable Battery Pack with Bare Wire connection
  D2F-FL Omron Snap Action Limit Switch with Level: Snap action switch with stainless steel lever.
